// Logisim project model.circ as structural Verilog: 2 circuits, main circuit 8-bit Computer
module _8_bit_Computer (
  input  in_1
);

  wire _0, _0_t, and_3_out, and_4_out, and_5_out, and_6_out, Clock, demultiplexer_1_out1,
       demultiplexer_1_out2, demultiplexer_1_out3, demultiplexer_1_out4, demultiplexer_1_out5,
       demultiplexer_1_out6, demultiplexer_1_out7, demultiplexer_1_out8, \if , Move, nor_1_out, not_1_out,
       not_2_out, not_3_out, not_4_out, not_5_out, not_6_out, not_7_out, or_1_out, or_2_out, or_3_out,
       or_4_out, Write;
  wire [3:0] Program_Counter_address, Program_Counter_address_2;
  wire [7:0] add_a_q, add_b_q, adder_1_out, Bus, controlled_buffer_1_out, Data, R1_q, R2_q, R3_q, R_Shift_q,
       ram_1_data, RAM_ADDR_q, shifter_1_out;
  wire [9:8] Program_Counter_address_3;
  wire [11:8] Program_Counter_instruction;

  Hex_Digit_Display hex_digit_display_1 (.value({2'b00, Program_Counter_address_3}));  // open: dp
  Hex_Digit_Display hex_digit_display_2 (.value(Program_Counter_address_2));  // open: dp
  Program_Counter Program_Counter (
    .Clock(Clock), .Reset(in_1), .Instruction({Program_Counter_instruction, Data}), .Condition(\if ),
    .Address({Program_Counter_address_3, Program_Counter_address_2, Program_Counter_address}));
  Hex_Digit_Display hex_digit_display_3 (.value(Program_Counter_address));  // open: dp
  Clock clock_1 (.out(Clock));
  Hex_Digit_Display hex_digit_display_4 (.value(Program_Counter_instruction));  // open: dp
  Hex_Digit_Display hex_digit_display_5 (.value(Data[7:4]));  // open: dp
  not not_1 (not_1_out, Program_Counter_instruction[10]);
  not not_2 (not_2_out, Program_Counter_instruction[11]);
  Demultiplexer #(.select(4)) demultiplexer_1 (
    .out0(_0), .out1(demultiplexer_1_out1), .out2(demultiplexer_1_out2), .out3(demultiplexer_1_out3),
    .out4(demultiplexer_1_out4), .out5(demultiplexer_1_out5), .out6(demultiplexer_1_out6),
    .out7(demultiplexer_1_out7), .out8(demultiplexer_1_out8), .out9(_0_t), .in(1'b1), .sel(Data[3:0]),
    .en(1'b1));  // open: out10, out11, out12, out13, out14, out15
  Hex_Digit_Display hex_digit_display_6 (.value(Data[3:0]));  // open: dp
  not not_3 (not_3_out, Program_Counter_instruction[11]);
  and and_1 (Write, not_1_out, not_2_out);
  LED led_1 (.in(Write));
  and and_2 (Move, Program_Counter_instruction[10], not_3_out);
  LED led_2 (.in(Move));
  assign controlled_buffer_1_out = Write ? Data : 8'bz;  // Controlled_Buffer controlled_buffer_1
  not not_4 (not_4_out, Write);
  nor nor_1 (nor_1_out, Bus[0], Bus[1], Bus[2], Bus[3], Bus[4], Bus[5], Bus[6], Bus[7]);
  not not_5 (not_5_out, Bus[7]);
  or or_1 (or_1_out, demultiplexer_1_out3, Write);
  assign controlled_buffer_1_out = not_4_out ? Bus : 8'bz;  // Controlled_Buffer controlled_buffer_2
  and and_3 (and_3_out, _0, nor_1_out);
  and and_4 (and_4_out, not_5_out, _0_t);
  Register add_a (.D(Bus), .en(demultiplexer_1_out7), .Q(add_a_q), .clk(and_6_out), .clr(in_1));
  Register add_b (.D(Bus), .en(demultiplexer_1_out8), .Q(add_b_q), .clk(and_6_out), .clr(in_1));
  Register R_Shift (.D(Bus), .en(demultiplexer_1_out4), .Q(R_Shift_q), .clk(and_6_out), .clr(in_1));
  Register R1 (.D(Bus), .en(demultiplexer_1_out1), .Q(R1_q), .clk(and_6_out), .clr(in_1));
  Register R2 (.D(Bus), .en(demultiplexer_1_out2), .Q(R2_q), .clk(and_6_out), .clr(in_1));
  Register R3 (.D(controlled_buffer_1_out), .en(or_1_out), .Q(R3_q), .clk(or_2_out), .clr(in_1));
  or or_2 (or_2_out, and_6_out, and_5_out);
  and and_5 (and_5_out, not_7_out, Write);
  and and_6 (and_6_out, Clock, Move);
  Register RAM_ADDR (.D(Bus), .en(demultiplexer_1_out5), .Q(RAM_ADDR_q), .clk(and_6_out), .clr(in_1));
  not not_6 (not_6_out, demultiplexer_1_out6);
  or or_3 (or_3_out, and_3_out, and_4_out);
  Adder adder_1 (.a(add_a_q), .b(add_b_q), .out(adder_1_out));  // open: cin, cout
  not not_7 (not_7_out, Clock);
  RAM #(.bus("separate")) ram_1 (
    .addr(RAM_ADDR_q), .din(Bus), .data(ram_1_data), .str(demultiplexer_1_out6), .clk(Clock), .ld(not_6_out),
    .clr(in_1));  // open: sel
  or or_4 (or_4_out, _0, _0_t);
  Register #(.width(1), .trigger("high")) u_If (.D(or_3_out), .Q(\if ), .clk(or_4_out), .clr(in_1));  // open: en
  Shifter #(.shift("lr")) shifter_1 (.in(R_Shift_q), .\dist (3'b001), .out(shifter_1_out));
  Multiplexer #(.select(4), .width(8)) multiplexer_1 (
    .in0(adder_1_out), .in1(R1_q), .in2(R2_q), .in3(R3_q), .in4(shifter_1_out), .in5(RAM_ADDR_q),
    .in6(ram_1_data), .out(Bus), .sel(Data[7:4]), .en(1'b1));  // open: in7, in8, in9, in10, in11, in12, in13, in14, in15

  // Other names for the same wires on the sheet: Reset = in_1; Source[3:0] = Data[7:4]; Target[3:0] = Data[3:0]

  // Notes on the sheet:
  //   ROM Address
  //   Instruction
  //   Data
  //   Write
endmodule

module Program_Counter (
  input  Reset,
  input  Clock,
  input  Condition,
  output [9:0] Address,
  output [11:0] Instruction
);

  wire and_1_out, and_2_out, not_1_out, not_2_out, or_1_out;
  wire [9:0] adder_1_out, controlled_buffer_1_out;

  assign controlled_buffer_1_out = and_1_out ? Instruction[9:0] : 10'bz;  // Controlled_Buffer controlled_buffer_1
  assign controlled_buffer_1_out = not_1_out ? adder_1_out : 10'bz;  // Controlled_Buffer controlled_buffer_2
  not not_1 (not_1_out, and_1_out);
  Register #(.width(10)) register_1 (.D(controlled_buffer_1_out), .Q(Address), .clk(Clock), .clr(Reset));  // open: en
  Adder #(.width(10)) adder_1 (.a(Address), .b(10'h1), .out(adder_1_out));  // open: cin, cout
  LED With_condition (.in(Instruction[10]));
  LED Jumping (.in(and_1_out));
  and and_1 (and_1_out, or_1_out, Instruction[11]);
  ROM #(.addrWidth(10), .dataWidth(12)) rom_1 (.addr(Address), .data(Instruction));  // open: sel
  or or_1 (or_1_out, not_2_out, and_2_out);
  not not_2 (not_2_out, Instruction[10]);
  and and_2 (and_2_out, Condition, Instruction[10]);

  // Notes on the sheet:
  //   contents of rom_1 (hex, n*v repeats v):
  //   411 1 437 438 407 804
endmodule
